# Fritzing sketch 03_AutoFlashLED (saved by Fritzing 0.9.2b)
breadboards: 1

parts:
  T-Cobbler1 = T-Cobbler
  module2 = AutoFlashLED

nets:
  N1: T-Cobbler1.5V0#20, module2.VCC
  N2: T-Cobbler1.GND#22, module2.GND

notes:
  Auto-flash LED

custom parts:
  T-Cobbler: T-Cobbler for RPi B+ and Rpi2 from SunFounder
  AutoFlashLED: Auto Flash LED module of SunFounder Sensor Kit
