# Fritzing sketch 04_Relay module (saved by Fritzing 0.9.2b)
breadboards: 1

parts:
  T-Cobbler1 = T-Cobbler
  module1 = Relay Module
  module2 = Dule-Color LED

nets:
  N1: T-Cobbler1.3V3#0, module1.VCC, module1.com
  N2: T-Cobbler1.GPIO17, module1.SIG
  GND: T-Cobbler1.GND#22, module1.GND, module2.GND
  N3: module1.on, module2.R
  N4: module1.off, module2.G

notes:
  Relay Module
  Dual-Color LED

custom parts:
  T-Cobbler: T-Cobbler for RPi B+ and Rpi2 from SunFounder
  Relay Module: Relay Module of SunFounder Sensor Kit
  Dule-Color LED: DuleColor LED module of SunFounder Sensor Kit
