# Fritzing sketch 06_Button (saved by Fritzing 0.9.2b)
breadboards: 1

parts:
  T-Cobbler1 = T-Cobbler
  module5 = Dule-Color LED
  module7 = Button

nets:
  N1: T-Cobbler1.3V3#0, module7.VCC
  N2: T-Cobbler1.GPIO17, module7.SIG
  N3: T-Cobbler1.GPIO27, module5.G
  GND: T-Cobbler1.GND#22, module5.GND, module7.GND
  N4: T-Cobbler1.GPIO18, module5.R

notes:
  Button
  Dual-color LED

custom parts:
  T-Cobbler: T-Cobbler for RPi B+ and Rpi2 from SunFounder
  Dule-Color LED: DuleColor LED module of SunFounder Sensor Kit
  Button: Button module of SunFounder Sensor Kit
