# Fritzing sketch 13_PCF8591 (saved by Fritzing 0.9.2b)
breadboards: 1

parts:
  T-Cobbler1 = T-Cobbler
  module5 = Dule-Color LED
  module10 = PCF8591

nets:
  N1: T-Cobbler1.3V3#0, module10.VCC
  N2: T-Cobbler1.SDA1, module10.SDA
  N3: T-Cobbler1.SCL1, module10.SCL
  GND: T-Cobbler1.GND#22, module5.GND, module10.GND
  N4: module5.R, module10.AO
  N5: module10.PM, module10.AIN0

notes:
  PCF8591
  Dual-color LED

custom parts:
  T-Cobbler: T-Cobbler for RPi B+ and Rpi2 from SunFounder
  Dule-Color LED: DuleColor LED module of SunFounder Sensor Kit
  PCF8591: PCF8591 ADC module for SunFounder Sensor Kit
