# Fritzing sketch 15_JoyStick_PS2 (saved by Fritzing 0.9.2b)
breadboards: 1

parts:
  T-Cobbler1 = T-Cobbler
  module10 = PCF8591
  module13 = JoyStick

nets:
  VCC: T-Cobbler1.3V3#0, module10.VCC, module13.VCC
  N1: T-Cobbler1.SDA1, module10.SDA
  N2: T-Cobbler1.SCL1, module10.SCL
  GND: T-Cobbler1.GND#22, module10.GND, module13.GND
  N3: module10.AIN1, module13.X
  N4: module10.AIN2, module13.BT
  N5: module10.AIN0, module13.Y

notes:
  PCF8591
  Joystick

custom parts:
  T-Cobbler: T-Cobbler for RPi B+ and Rpi2 from SunFounder
  PCF8591: PCF8591 ADC module for SunFounder Sensor Kit
  JoyStick: JoyStick module of SunFounder Sensor Kit
