# Fritzing sketch 16_Potentiometer (saved by Fritzing 0.9.2b)
breadboards: 1

parts:
  T-Cobbler1 = T-Cobbler
  module10 = PCF8591
  module15 = Potentiometer
  module16 = Dule-Color LED

nets:
  VCC: T-Cobbler1.3V3#0, module10.VCC, module15.VCC
  N1: T-Cobbler1.SDA1, module10.SDA
  N2: T-Cobbler1.SCL1, module10.SCL
  GND: T-Cobbler1.GND#22, module10.GND, module15.GND, module16.GND
  N3: module10.AO, module16.R
  N4: module10.AIN0, module15.SIG

notes:
  PCF8591
  Potentiometer
  Dual-Color LED

custom parts:
  T-Cobbler: T-Cobbler for RPi B+ and Rpi2 from SunFounder
  PCF8591: PCF8591 ADC module for SunFounder Sensor Kit
  Potentiometer: Potentiometer module of SunFounder Sensor Kit
  Dule-Color LED: DuleColor LED module of SunFounder Sensor Kit
