# Fritzing sketch 18_Analog_Temperature (saved by Fritzing 0.8.7b)
breadboards: 1

parts:
  T-Cobbler1 = T-Cobbler
  module10 = PCF8591
  module16 = Analog Temperature

nets:
  VCC: T-Cobbler1.3V3#0, module10.VCC, module16.VCC
  N1: T-Cobbler1.SDA1, module10.SDA
  N2: T-Cobbler1.SCL1, module10.SCL
  N3: T-Cobbler1.GPIO17, module16.DO
  GND: T-Cobbler1.GND#22, module10.GND, module16.GND
  N4: module10.AIN0, module16.AO

notes:
  PCF8591
  Analog Temperature Sensor

custom parts:
  T-Cobbler: T-Cobbler for RPi B+ and Rpi2 from SunFounder
  PCF8591: PCF8591 ADC module for SunFounder Sensor Kit
  Analog Temperature: Analog Temperature module of SunFounder Sensor Kit
