# Fritzing sketch 18_Thermistor (saved by Fritzing 0.9.2b)
breadboards: 1

parts:
  T-Cobbler1 = T-Cobbler
  module10 = PCF8591
  module17 = Thermistor

nets:
  VCC: T-Cobbler1.3V3#0, module10.VCC, module17.VCC
  N1: T-Cobbler1.SDA1, module10.SDA
  N2: T-Cobbler1.SCL1, module10.SCL
  GND: T-Cobbler1.GND#22, module10.GND, module17.GND
  N3: module10.AIN0, module17.SIG

notes:
  PCF8591
  Thermistor

custom parts:
  T-Cobbler: T-Cobbler for RPi B+ and Rpi2 from SunFounder
  PCF8591: PCF8591 ADC module for SunFounder Sensor Kit
  Thermistor: Thermistor module of SunFounder Sensor Kit
