# Fritzing sketch 19_Sound Sensor (saved by Fritzing 0.9.2b)
breadboards: 1

parts:
  T-Cobbler1 = T-Cobbler
  module10 = PCF8591
  module18 = Sound Sensor

nets:
  VCC: T-Cobbler1.3V3#0, module10.VCC, module18.VCC
  N1: T-Cobbler1.SDA1, module10.SDA
  N2: T-Cobbler1.SCL1, module10.SCL
  GND: T-Cobbler1.GND#22, module10.GND, module18.GND
  N3: module10.AIN0, module18.SIG

notes:
  PCF8591
  Sound Sensor

custom parts:
  T-Cobbler: T-Cobbler for RPi B+ and Rpi2 from SunFounder
  PCF8591: PCF8591 ADC module for SunFounder Sensor Kit
  Sound Sensor: Sound Sensor module of SunFounder Sensor Kit
