# Fritzing sketch 21_Flame_Sensor (saved by Fritzing 0.9.2b)
breadboards: 1

parts:
  T-Cobbler1 = T-Cobbler
  module10 = PCF8591
  module20 = Flame Sensor

nets:
  VCC: T-Cobbler1.3V3#0, module10.VCC, module20.VCC
  N1: T-Cobbler1.SDA1, module10.SDA
  N2: T-Cobbler1.SCL1, module10.SCL
  N3: T-Cobbler1.GPIO17, module20.DO
  GND: T-Cobbler1.GND#22, module10.GND, module20.GND
  N4: module10.AIN0, module20.AO

notes:
  PCF8591
  Flame Sensor

custom parts:
  T-Cobbler: T-Cobbler for RPi B+ and Rpi2 from SunFounder
  PCF8591: PCF8591 ADC module for SunFounder Sensor Kit
  Flame Sensor: Flame Sensor module of SunFounder Sensor Kit
