# Fritzing sketch 23_IR remote control (saved by Fritzing 0.9.2b)
breadboards: 1

parts:
  T-Cobbler1 = T-Cobbler
  module8 = IR Receiver
  module9 = RGB LED

nets:
  N1: T-Cobbler1.GPIO17, module9.R
  N2: T-Cobbler1.GPIO27, module9.B
  VCC: T-Cobbler1.5V0#20, module8.VCC, module9.VCC
  N3: T-Cobbler1.GND#22, module8.GND
  N4: T-Cobbler1.GPIO18, module9.G
  N5: T-Cobbler1.GPIO23, module8.SIG

notes:
  IR Receiver
  RGB LED

custom parts:
  T-Cobbler: T-Cobbler for RPi B+ and Rpi2 from SunFounder
  IR Receiver: IR Receiver module of SunFounder Sensor Kit
  RGB LED: RGB LED module of SunFounder Sensor Kit
