# Fritzing sketch 24_Touch_Switch (saved by Fritzing 0.9.2b)
breadboards: 1

parts:
  T-Cobbler1 = T-Cobbler
  module5 = Dule-Color LED
  module6 = Touch Switch

nets:
  N1: T-Cobbler1.GPIO17, module6.SIG
  N2: T-Cobbler1.GPIO27, module5.G
  N3: T-Cobbler1.5V0#20, module6.VCC
  GND: T-Cobbler1.GND#22, module5.GND, module6.GND
  N4: T-Cobbler1.GPIO18, module5.R

notes:
  Touch Switch
  Dual-color LED

custom parts:
  T-Cobbler: T-Cobbler for RPi B+ and Rpi2 from SunFounder
  Dule-Color LED: DuleColor LED module of SunFounder Sensor Kit
  Touch Switch: Touch Switch module of SunFounder Sensor Kit
