# Fritzing sketch 25_Ultrasonic_Ranging (saved by Fritzing 0.8.7b)
breadboards: 1

parts:
  T-Cobbler1 = T-Cobbler
  module3 = Ultrasonic-HC-SRO4

nets:
  N1: T-Cobbler1.GPIO17, module3.TRIG
  N2: T-Cobbler1.5V0#20, module3.VCC
  N3: T-Cobbler1.GND#22, module3.GND
  N4: T-Cobbler1.GPIO18, module3.ECHO

custom parts:
  T-Cobbler: T-Cobbler for RPi B+ and Rpi2 from SunFounder
  Ultrasonic-HC-SRO4: The ultrasonic sensor uses sound to accurately detect objects and measure distances. It sends out ultrasonic waves and converts them into electronic signals
