# Fritzing sketch 28_Humiture (saved by Fritzing 0.9.3b)
breadboards: 1

parts:
  T-Cobbler1 = T-Cobbler
  module3 = DHT11 Humiture Sensor

nets:
  N1: T-Cobbler1.3V3#0, module3.VCC
  N2: T-Cobbler1.GND#4, module3.GND
  N3: T-Cobbler1.GPIO17, module3.SIG

notes:
  Huimiture Sensor

custom parts:
  T-Cobbler: T-Cobbler for RPi B+ and Rpi2 from SunFounder
  DHT11 Humiture Sensor: DHT11 Humiture Sensor module of SunFounder Sensor Kit
