# Fritzing sketch 29_IR Obstacle (saved by Fritzing 0.9.3b)
breadboards: 1

parts:
  T-Cobbler1 = T-Cobbler
  module4 = IR Obstacle

nets:
  N1: T-Cobbler1.3V3#0, module4.VCC
  N2: T-Cobbler1.GND#4, module4.GND
  N3: T-Cobbler1.GPIO17, module4.SIG

notes:
  IR Obstacle

custom parts:
  T-Cobbler: T-Cobbler for RPi B+ and Rpi2 from SunFounder
  IR Obstacle: IR Obstacle module of SunFounder Sensor Kit.
