# Fritzing sketch 31_Barometer (saved by Fritzing 0.9.3b)
breadboards: 1

parts:
  T-Cobbler1 = T-Cobbler
  module6 = Barometer

nets:
  N1: T-Cobbler1.SDA1, module6.SDA
  N2: T-Cobbler1.SCL1, module6.SCL
  N3: T-Cobbler1.3V3#8, module6.VCC
  N4: T-Cobbler1.GND#12, module6.GND

notes:
  Barometer

custom parts:
  T-Cobbler: T-Cobbler for RPi B+ and Rpi2 from SunFounder
  Barometer: barometer module of SunFounder Sensor Kit
